// Logisim project 4-bit register.circ as structural Verilog: 1 circuit, main circuit main
module main (
  input  in_1,
  input  in_2,
  input  in_3,
  input  in_4,
  input  in_5,
  output out_6,
  output out_7,
  output out_8,
  output out_9
);

  wire clock_1_out, not_1_out, not_2_out, not_3_out, not_4_out;

  Clock clock_1 (.out(clock_1_out));
  not not_1 (not_1_out, in_5);
  not not_2 (not_2_out, in_5);
  D_Flip_Flop d_ff_1 (.clk(clock_1_out), .D(in_1), .Q(out_6), .en(not_1_out));  // open: Qn, preset, reset
  D_Flip_Flop d_ff_2 (.clk(clock_1_out), .D(in_2), .Q(out_7), .en(not_3_out));  // open: Qn, preset, reset
  not not_3 (not_3_out, in_5);
  D_Flip_Flop d_ff_3 (.clk(clock_1_out), .D(in_3), .Q(out_8), .en(not_2_out));  // open: Qn, preset, reset
  D_Flip_Flop d_ff_4 (.clk(clock_1_out), .D(in_4), .Q(out_9), .en(not_4_out));  // open: Qn, preset, reset
  not not_4 (not_4_out, in_5);
endmodule
