// Logisim project 4-bit synchronous binary counter.circ as structural Verilog: 1 circuit, main circuit main
module main (
  input  Count_enable,
  output A0,
  output A1,
  output A2,
  output A3,
  output Output_carry
);

  wire and_1_out, and_2_out, and_3_out, Clock_out;

  and and_1 (and_1_out, Count_enable, A0);
  and and_2 (and_2_out, and_1_out, A1);
  and and_3 (and_3_out, and_2_out, A2);
  Clock Clock (.out(Clock_out));
  J_K_Flip_Flop j_k_ff_1 (.J(Count_enable), .clk(Clock_out), .K(Count_enable), .Q(A0));  // open: Qn, preset, en, reset
  J_K_Flip_Flop j_k_ff_2 (.J(and_1_out), .clk(Clock_out), .K(and_1_out), .Q(A1));  // open: Qn, preset, en, reset
  J_K_Flip_Flop j_k_ff_3 (.J(and_2_out), .clk(Clock_out), .K(and_2_out), .Q(A2));  // open: Qn, preset, en, reset
  J_K_Flip_Flop j_k_ff_4 (.J(and_3_out), .clk(Clock_out), .K(and_3_out), .Q(A3));  // open: Qn, preset, en, reset
  and and_4 (Output_carry, A3, and_3_out);
endmodule
