// Logisim project 9linePriorityEncoder.circ as structural Verilog: 1 circuit, main circuit main
module main (
  input  _1,
  input  _2,
  input  _3,
  input  _4,
  input  _5,
  input  _6,
  input  _7,
  input  _8,
  input  _9
);

  wire j10_out, j11_out, j12_out, j13_out, j14_out, j15_out, j16_out, j17_out, not_1_out, not_2_out,
       not_3_out, not_4_out, not_5_out, not_6_out, not_7_out, not_8_out, not_9_out, not_10_out, u1_out,
       u2_out, u3_out, u4_out, u5_out, u6_out, u7_out, u8_out, u9_out;

  not not_1 (not_1_out, _2);
  not not_2 (not_2_out, _4);
  not not_3 (not_3_out, _5);
  not not_4 (not_4_out, _4);
  not not_5 (not_5_out, _4);
  not not_6 (not_6_out, _6);
  not not_7 (not_7_out, _6);
  not not_8 (not_8_out, _4);
  not not_9 (not_9_out, _5);
  nor j16 (j16_out, _8, _9);
  not not_10 (not_10_out, _6);
  and u1 (u1_out, _1, not_1_out, not_5_out, not_10_out, j16_out);
  and u2 (u2_out, _3, not_2_out, not_6_out, j16_out);
  and u3 (u3_out, _5, not_7_out, j16_out);
  and u4 (u4_out, _7, j16_out);
  and u5 (u5_out, _2, not_8_out, not_3_out, j16_out);
  and u6 (u6_out, not_4_out, not_9_out, _3, j16_out);
  and u7 (u7_out, _6, j16_out);
  and u8 (u8_out, _7, j16_out);
  and u9 (u9_out, _4, j16_out);
  and j10 (j10_out, _5, j16_out);
  and j11 (j11_out, _6, j16_out);
  and j12 (j12_out, _7, j16_out);
  or j17 (j17_out, _8, _9);
  or j13 (j13_out, u1_out, u2_out, u3_out, u4_out);
  LED led_1 (.in(j13_out));
  or j14 (j14_out, u5_out, u6_out, u7_out, u8_out);
  LED led_2 (.in(j14_out));
  or j15 (j15_out, u9_out, j10_out, j11_out, j12_out);
  LED led_3 (.in(j17_out));
  LED led_4 (.in(j15_out));
endmodule
