// Logisim project 9linePriorityEncodeupdateversion.circ as structural Verilog: 1 circuit, main circuit main
module main (
  input  _1,
  input  _2,
  input  _3,
  input  _4,
  input  _5,
  input  _6,
  input  _7,
  input  _8,
  input  _9,
  output output1,
  output output2,
  output output3,
  output output4
);

  wire j16_out, not_1_out, not_2_out, not_3_out, not_4_out, not_5_out, not_6_out, not_7_out, not_8_out,
       not_9_out, not_10_out, u1_out, u2_out, u3_out, u4_out, u5_out, u6_out, u7_out, u8_out, u9_out,
       u10_out, u11_out, u12_out;

  not not_1 (not_1_out, _2);
  not not_2 (not_2_out, _4);
  not not_3 (not_3_out, _6);
  not not_4 (not_4_out, _4);
  not not_5 (not_5_out, _4);
  not not_6 (not_6_out, _4);
  not not_7 (not_7_out, _6);
  not not_8 (not_8_out, _6);
  not not_9 (not_9_out, _5);
  not not_10 (not_10_out, _5);
  nor j16 (j16_out, _8, _9);
  and u1 (u1_out, _1, not_1_out, not_6_out, not_7_out, j16_out);
  and u2 (u2_out, _3, not_2_out, not_8_out, j16_out);
  and u3 (u3_out, _5, not_3_out, j16_out);
  and u4 (u4_out, _7, j16_out);
  and u5 (u5_out, _2, not_4_out, not_9_out, j16_out);
  and u6 (u6_out, _3, not_5_out, not_10_out, j16_out);
  and u7 (u7_out, _6, j16_out);
  and u8 (u8_out, _7, j16_out);
  and u9 (u9_out, _4, j16_out);
  and u10 (u10_out, _5, j16_out);
  and u11 (u11_out, _6, j16_out);
  and u12 (u12_out, _7, j16_out);
  or j17 (output4, _8, _9);
  or j13 (output1, u1_out, u2_out, u3_out, u4_out, _9);
  or j14 (output2, u5_out, u6_out, u7_out, u8_out);
  or j15 (output3, u9_out, u10_out, u11_out, u12_out);
endmodule
