// Logisim project Construct a 5-to-32-line decoder with four 3-to-8-line decoders with enable and a 2-to- 4.circ as structural Verilog: 1 circuit, main circuit main
module main (
  input  [2:0] A2_A1_A0,
  input  [1:0] A4_A3,
  output D0,
  output out_4,
  output out_5,
  output out_6,
  output out_7,
  output out_8,
  output out_9,
  output out_10,
  output D8,
  output out_12,
  output out_13,
  output out_14,
  output out_15,
  output out_16,
  output out_17,
  output out_18,
  output D16,
  output out_20,
  output out_21,
  output out_22,
  output out_23,
  output out_24,
  output out_25,
  output out_26,
  output D24,
  output out_28,
  output out_29,
  output out_30,
  output out_31,
  output out_32,
  output out_33,
  output out_34
);

  wire decoder_1_out0, decoder_1_out1, decoder_1_out2, decoder_1_out3;

  Decoder #(.select(2), .enable("false")) decoder_1 (
    .out0(decoder_1_out0), .out1(decoder_1_out1), .out2(decoder_1_out2), .out3(decoder_1_out3), .sel(A4_A3));
  Decoder #(.select(3)) decoder_2 (
    .out0(D0), .out1(out_4), .out2(out_5), .out3(out_6), .out4(out_7), .out5(out_8), .out6(out_9),
    .out7(out_10), .sel(A2_A1_A0), .en(decoder_1_out0));
  Decoder #(.select(3)) decoder_3 (
    .out0(D8), .out1(out_12), .out2(out_13), .out3(out_14), .out4(out_15), .out5(out_16), .out6(out_17),
    .out7(out_18), .sel(A2_A1_A0), .en(decoder_1_out1));
  Decoder #(.select(3)) decoder_4 (
    .out0(D16), .out1(out_20), .out2(out_21), .out3(out_22), .out4(out_23), .out5(out_24), .out6(out_25),
    .out7(out_26), .sel(A2_A1_A0), .en(decoder_1_out2));
  Decoder #(.select(3)) decoder_5 (
    .out0(D24), .out1(out_28), .out2(out_29), .out3(out_30), .out4(out_31), .out5(out_32), .out6(out_33),
    .out7(out_34), .sel(A2_A1_A0), .en(decoder_1_out3));
endmodule
