// Logisim project Encoder.circ as structural Verilog: 1 circuit, main circuit main
module main (
  input  d0,
  input  d1,
  input  d2,
  input  d3,
  input  d4,
  input  d5,
  input  d6,
  input  d7
);

  wire or_1_out, or_2_out, or_3_out;

  or or_1 (or_1_out, d1, d3, d5, d7);
  or or_2 (or_2_out, d2, d3, d6, d7);
  or or_3 (or_3_out, d4, d5, d6, d7);
  LED a0 (.in(or_1_out));
  LED a1 (.in(or_2_out));
  LED a2 (.in(or_3_out));

  // Notes on the sheet:
  //   LSB = LEAST SIGNIFICANT BIT
  //   MSB = MOST SIGNIFICANT BIT
  //   LSB(RIGHT SIDE)
  //   MSB (LEFT SIDE)
endmodule
