// Logisim project decoders.circ as structural Verilog: 1 circuit, main circuit main
// I0
module main (
  input  [1:0] Y___X,
  input  Z_enable_gate,
  output D0,
  output D1,
  output D2,
  output D3,
  output D4,
  output D5,
  output D6,
  output D7
);

  wire not_1_out;

  not not_1 (not_1_out, Z_enable_gate);
  Decoder #(.select(2)) decoder_1 (.out0(D0), .out1(D1), .out2(D2), .out3(D3), .sel(Y___X), .en(not_1_out));
  Decoder #(.select(2)) decoder_2 (.out0(D4), .out1(D5), .out2(D6), .out3(D7), .sel(Y___X), .en(Z_enable_gate));
endmodule
